// Logisim project CRC.circ as structural Verilog
module _4bit_div (
  input  [3:0] A,
  input  [3:0] B,
  output [2:0] out_3
);

  wire not_1_out;
  wire [2:0] xor_1_out;

  xor xor_1 (xor_1_out[0], A[0], B[0]);
  xor xor_2 (xor_1_out[1], A[1], B[1]);
  xor xor_3 (xor_1_out[2], A[2], B[2]);
  Multiplexer #(.width(3)) multiplexer_1 (.in0(xor_1_out), .in1(A[2:0]), .out(out_3), .sel(not_1_out));  // open: en
  not not_1 (not_1_out, A[3]);
endmodule

module CRC (
  input  [7:0] A,
  input  [3:0] B,
  output [10:0] out_3
);

  wire [3:1] n4bit_div_1_out_3, n4bit_div_2_out_3, n4bit_div_3_out_3, n4bit_div_4_out_3, n4bit_div_5_out_3,
       n4bit_div_6_out_3, n4bit_div_7_out_3;

  // Probe on n4bit_div_1_out_3
  // Probe on A[7:4]
  _4bit_div u_4bit_div_1 (.A(A[7:4]), .B(B), .out_3(n4bit_div_1_out_3));
  _4bit_div u_4bit_div_2 (.A({n4bit_div_1_out_3, A[3]}), .B(B), .out_3(n4bit_div_2_out_3));
  _4bit_div u_4bit_div_3 (.A({n4bit_div_2_out_3, A[2]}), .B(B), .out_3(n4bit_div_3_out_3));
  _4bit_div u_4bit_div_4 (.A({n4bit_div_3_out_3, A[1]}), .B(B), .out_3(n4bit_div_4_out_3));
  _4bit_div u_4bit_div_5 (.A({n4bit_div_4_out_3, A[0]}), .B(B), .out_3(n4bit_div_5_out_3));
  _4bit_div u_4bit_div_6 (.A({n4bit_div_5_out_3, 1'b0}), .B(B), .out_3(n4bit_div_6_out_3));
  _4bit_div u_4bit_div_7 (.A({n4bit_div_6_out_3, 1'b0}), .B(B), .out_3(n4bit_div_7_out_3));
  _4bit_div u_4bit_div_8 (.A({n4bit_div_7_out_3, 1'b0}), .B(B), .out_3(out_3[2:0]));

  assign out_3[10:3] = A;
endmodule
