// Logisim project FSM.circ as structural Verilog: 3 circuits, main circuit main
module main (
  input  clr,
  input  [1:0] In,
  output out_3
);

  wire and_1_out, clock_1_out, pro_1_out_4, pro_1_out_5, pro_1_out_6;
  wire [1:0] data, multiplexer_1_out, register_1_q;

  Multiplexer #(.width(2)) multiplexer_1 (.in0(data), .in1(2'b00), .out(multiplexer_1_out), .sel(clr));  // open: en
  Register #(.width(2)) register_1 (.D(multiplexer_1_out), .Q(register_1_q), .clk(clock_1_out));  // open: en, clr
  Clock clock_1 (.out(clock_1_out));
  pro pro_1 (
    .in(In), .state(register_1_q), .out_6(pro_1_out_6), .out_3(data), .out_4(pro_1_out_4), .out_5(pro_1_out_5));
  and and_1 (and_1_out, pro_1_out_4, pro_1_out_6);
  or or_1 (out_3, and_1_out, pro_1_out_5);
endmodule

module pro (
  input  [1:0] in,
  input  [1:0] state,
  output [1:0] out_3,
  output out_4,
  output out_5,
  output out_6
);

  wire a, and_1_out, and_2_out, and_3_out, and_4_out, and_5_out, and_6_out, and_7_out, and_8_out, and_9_out,
       and_10_out, and_11_out, and_12_out, and_13_out, b, c, o, or_2_out, or_3_out, or_4_out, or_5_out, S0,
       S1;
  wire [1:0] multiplexer_1_out, multiplexer_2_out, multiplexer_3_out, multiplexer_4_out;

  Demultiplexer #(.select(2)) demultiplexer_1 (
    .out0(a), .out1(b), .out2(c), .out3(o), .in(1'b1), .sel(in));  // open: en
  Demultiplexer #(.select(2)) demultiplexer_2 (
    .out0(S0), .out1(S1), .out2(out_4), .out3(out_5), .in(1'b1), .sel(state));  // open: en
  or or_1 (out_6, a, c);
  and and_1 (and_1_out, S0, b);
  and and_2 (and_2_out, S1, b);
  and and_3 (and_3_out, S1, a);
  and and_4 (and_4_out, S1, c);
  and and_5 (and_5_out, S1, o);
  and and_6 (and_6_out, out_4, b);
  and and_7 (and_7_out, out_4, a);
  and and_8 (and_8_out, out_4, c);
  and and_9 (and_9_out, out_4, o);
  and and_10 (and_10_out, out_5, b);
  and and_11 (and_11_out, out_5, a);
  and and_12 (and_12_out, out_5, c);
  and and_13 (and_13_out, out_5, o);
  or or_2 (or_2_out, and_5_out, and_9_out, and_11_out, and_12_out, and_13_out);
  or or_3 (or_3_out, and_1_out, and_2_out, and_6_out, and_10_out);
  Multiplexer #(.width(2)) multiplexer_1 (
    .in0(2'b00), .in1(2'b00), .out(multiplexer_1_out), .sel(or_2_out));  // open: en
  Multiplexer #(.width(2)) multiplexer_2 (
    .in0(2'b00), .in1(2'b01), .out(multiplexer_2_out), .sel(or_3_out));  // open: en
  or or_4 (or_4_out, and_3_out, and_4_out);
  Multiplexer #(.width(2)) multiplexer_3 (
    .in0(2'b00), .in1(2'b10), .out(multiplexer_3_out), .sel(or_4_out));  // open: en
  Multiplexer #(.width(2)) multiplexer_4 (
    .in0(2'b00), .in1(2'b11), .out(multiplexer_4_out), .sel(or_5_out));  // open: en
  or or_5 (or_5_out, and_7_out, and_8_out);
  assign out_3 = multiplexer_1_out | multiplexer_2_out | multiplexer_3_out | multiplexer_4_out;  // OR_Gate or_6, 2 bits wide

  // Other names for the same wires on the sheet: s[1:0] = state; S2 = out_4; S3 = out_5
endmodule

module fsm (
  input  clr,
  input  [1:0] In,
  output out_3
);

  wire clock_1_out, pro_1_out_4, pro_1_out_6;
  wire [1:0] data, multiplexer_1_out, register_1_q;

  Multiplexer #(.width(2)) multiplexer_1 (.in0(data), .in1(2'b00), .out(multiplexer_1_out), .sel(clr));  // open: en
  Register #(.width(2)) register_1 (.D(multiplexer_1_out), .Q(register_1_q), .clk(clock_1_out));  // open: en, clr
  Clock clock_1 (.out(clock_1_out));
  pro pro_1 (.in(In), .state(register_1_q), .out_6(pro_1_out_6), .out_3(data), .out_4(pro_1_out_4));  // open: out_5
  and and_1 (out_3, pro_1_out_4, pro_1_out_6);
endmodule
