// Logisim project GRF.circ as structural Verilog
module grf (
  input  clk,
  input  reset,
  input  WE,
  input  [4:0] A1,
  input  [4:0] A2,
  input  [4:0] A3,
  input  [31:0] WD,
  output [31:0] out_8,
  output [31:0] out_9
);

  wire W1, W2, W3, W4, W5, W6, W7, W8, W9, W10, W11, W12, W13, W14, W15, W16, W17, W18, W19, W20, W21, W22,
       W23, W24, W25, W26, W27, W28, W29, W30, W31;
  wire [31:0] _0, _1, _2, _3, _4, _5, _6, _7, _8, _9, _10, _11, _12, _13, _14, _15, _16, _17, _18, _19, _20,
       _21, _22, _23, _24, _25, _26, _27, _28, _29, _30, _31;

  Register #(.width(32)) register_1 (.D(WD), .Q(_0), .clk(clk), .clr(reset));  // open: en
  Register #(.width(32)) register_2 (.D(WD), .en(W1), .Q(_1), .clk(clk), .clr(reset));
  Register #(.width(32)) register_3 (.D(WD), .en(W2), .Q(_2), .clk(clk), .clr(reset));
  Register #(.width(32)) register_4 (.D(WD), .en(W3), .Q(_3), .clk(clk), .clr(reset));
  Register #(.width(32)) register_5 (.D(WD), .en(W4), .Q(_4), .clk(clk), .clr(reset));
  Demultiplexer #(.select(5)) demultiplexer_1 (
    .out1(W1), .out2(W2), .out3(W3), .out4(W4), .out5(W5), .out6(W6), .out7(W7), .out8(W8), .out9(W9),
    .out10(W10), .out11(W11), .out12(W12), .out13(W13), .out14(W14), .out15(W15), .out16(W16), .out17(W17),
    .out18(W18), .out19(W19), .out20(W20), .out21(W21), .out22(W22), .out23(W23), .out24(W24), .out25(W25),
    .out26(W26), .out27(W27), .out28(W28), .out29(W29), .out30(W30), .out31(W31), .in(WE), .sel(A3));  // open: out0, en
  Register #(.width(32)) register_6 (.D(WD), .en(W5), .Q(_5), .clk(clk), .clr(reset));
  Register #(.width(32)) register_7 (.D(WD), .en(W6), .Q(_6), .clk(clk), .clr(reset));
  Register #(.width(32)) register_8 (.D(WD), .en(W7), .Q(_7), .clk(clk), .clr(reset));
  Register #(.width(32)) register_9 (.D(WD), .en(W8), .Q(_8), .clk(clk), .clr(reset));
  Register #(.width(32)) register_10 (.D(WD), .en(W9), .Q(_9), .clk(clk), .clr(reset));
  Register #(.width(32)) register_11 (.D(WD), .en(W10), .Q(_10), .clk(clk), .clr(reset));
  Register #(.width(32)) register_12 (.D(WD), .en(W11), .Q(_11), .clk(clk), .clr(reset));
  Register #(.width(32)) register_13 (.D(WD), .en(W12), .Q(_12), .clk(clk), .clr(reset));
  Register #(.width(32)) register_14 (.D(WD), .en(W13), .Q(_13), .clk(clk), .clr(reset));
  Register #(.width(32)) register_15 (.D(WD), .en(W14), .Q(_14), .clk(clk), .clr(reset));
  Register #(.width(32)) register_16 (.D(WD), .en(W15), .Q(_15), .clk(clk), .clr(reset));
  Register #(.width(32)) register_17 (.D(WD), .en(W16), .Q(_16), .clk(clk), .clr(reset));
  Register #(.width(32)) register_18 (.D(WD), .en(W17), .Q(_17), .clk(clk), .clr(reset));
  Register #(.width(32)) register_19 (.D(WD), .en(W18), .Q(_18), .clk(clk), .clr(reset));
  Register #(.width(32)) register_20 (.D(WD), .en(W19), .Q(_19), .clk(clk), .clr(reset));
  Register #(.width(32)) register_21 (.D(WD), .en(W20), .Q(_20), .clk(clk), .clr(reset));
  Register #(.width(32)) register_22 (.D(WD), .en(W21), .Q(_21), .clk(clk), .clr(reset));
  Register #(.width(32)) register_23 (.D(WD), .en(W22), .Q(_22), .clk(clk), .clr(reset));
  Register #(.width(32)) register_24 (.D(WD), .en(W23), .Q(_23), .clk(clk), .clr(reset));
  Register #(.width(32)) register_25 (.D(WD), .en(W24), .Q(_24), .clk(clk), .clr(reset));
  Register #(.width(32)) register_26 (.D(WD), .en(W25), .Q(_25), .clk(clk), .clr(reset));
  Register #(.width(32)) register_27 (.D(WD), .en(W26), .Q(_26), .clk(clk), .clr(reset));
  Register #(.width(32)) register_28 (.D(WD), .en(W27), .Q(_27), .clk(clk), .clr(reset));
  Register #(.width(32)) register_29 (.D(WD), .en(W28), .Q(_28), .clk(clk), .clr(reset));
  Register #(.width(32)) register_30 (.D(WD), .en(W29), .Q(_29), .clk(clk), .clr(reset));
  Register #(.width(32)) register_31 (.D(WD), .en(W30), .Q(_30), .clk(clk), .clr(reset));
  Register #(.width(32)) register_32 (.D(WD), .en(W31), .Q(_31), .clk(clk), .clr(reset));
  Multiplexer #(.select(5), .width(32)) multiplexer_1 (
    .in0(_0), .in1(_1), .in2(_2), .in3(_3), .in4(_4), .in5(_5), .in6(_6), .in7(_7), .in8(_8), .in9(_9),
    .in10(_10), .in11(_11), .in12(_12), .in13(_13), .in14(_14), .in15(_15), .in16(_16), .in17(_17),
    .in18(_18), .in19(_19), .in20(_20), .in21(_21), .in22(_22), .in23(_23), .in24(_24), .in25(_25),
    .in26(_26), .in27(_27), .in28(_28), .in29(_29), .in30(_30), .in31(_31), .out(out_8), .sel(A1));  // open: en
  Multiplexer #(.select(5), .width(32)) multiplexer_2 (
    .in0(_0), .in1(_1), .in2(_2), .in3(_3), .in4(_4), .in5(_5), .in6(_6), .in7(_7), .in8(_8), .in9(_9),
    .in10(_10), .in11(_11), .in12(_12), .in13(_13), .in14(_14), .in15(_15), .in16(_16), .in17(_17),
    .in18(_18), .in19(_19), .in20(_20), .in21(_21), .in22(_22), .in23(_23), .in24(_24), .in25(_25),
    .in26(_26), .in27(_27), .in28(_28), .in29(_29), .in30(_30), .in31(_31), .out(out_9), .sel(A2));  // open: en

  // Other names for the same wires on the sheet: Data[31:0] = WD
endmodule
