// Logisim project GRF_.circ as structural Verilog
module grf (
  input  reset,
  input  WE,
  input  [4:0] A1,
  input  [4:0] A2,
  input  [4:0] A3,
  input  [31:0] WD,
  output [31:0] out_7,
  output [31:0] out_8
);

  wire clock_1_out, demultiplexer_1_out1, demultiplexer_1_out2, demultiplexer_1_out3, demultiplexer_1_out4,
       demultiplexer_1_out5, demultiplexer_1_out6, demultiplexer_1_out7, demultiplexer_1_out8,
       demultiplexer_1_out9, demultiplexer_1_out10, demultiplexer_1_out11, demultiplexer_1_out12,
       demultiplexer_1_out13, demultiplexer_1_out14, demultiplexer_1_out15, demultiplexer_1_out16,
       demultiplexer_1_out17, demultiplexer_1_out18, demultiplexer_1_out19, demultiplexer_1_out20,
       demultiplexer_1_out21, demultiplexer_1_out22, demultiplexer_1_out23, demultiplexer_1_out24,
       demultiplexer_1_out25, demultiplexer_1_out26, demultiplexer_1_out27, demultiplexer_1_out28,
       demultiplexer_1_out29, demultiplexer_1_out30, demultiplexer_1_out31, reset_t, undriven, undriven_2,
       undriven_3, undriven_4, undriven_5, undriven_6, undriven_7, undriven_8, undriven_9, undriven_10,
       undriven_11, undriven_12, undriven_13, undriven_14, undriven_15, undriven_16, undriven_17,
       undriven_18, undriven_19, undriven_20, undriven_21, undriven_22, undriven_23, undriven_24,
       undriven_25, undriven_26, undriven_27, undriven_28, undriven_29, undriven_30, W1, W2, W3, W4, W5, W6,
       W7, W8, W9, W10, W11, W12, W13, W14, W15, W16, W17, W18, W19, W20, W21, W22, W23, W24, W25, W26, W27,
       W28, W29, W30, W31, WE_t;
  wire [31:0] _0, _1, _2, _3, _4, _5, _6, _7, _8, _9, _10, _11, _12, _13, _14, _15, _16, _17, _18, _19, _20,
       _21, _22, _23, _24, _25, _26, _27, _28, _29, _30, _31, Data;

  // Probe on Data
  Multiplexer #(.width(32)) multiplexer_1 (.in0(WD), .in1({32{1'b0}}), .out(Data), .sel(reset));  // open: en
  Clock clock_1 (.out(clock_1_out));
  Demultiplexer #(.select(5)) demultiplexer_1 (
    .out1(demultiplexer_1_out1), .out2(demultiplexer_1_out2), .out3(demultiplexer_1_out3),
    .out4(demultiplexer_1_out4), .out5(demultiplexer_1_out5), .out6(demultiplexer_1_out6),
    .out7(demultiplexer_1_out7), .out8(demultiplexer_1_out8), .out9(demultiplexer_1_out9),
    .out10(demultiplexer_1_out10), .out11(demultiplexer_1_out11), .out12(demultiplexer_1_out12),
    .out13(demultiplexer_1_out13), .out14(demultiplexer_1_out14), .out15(demultiplexer_1_out15),
    .out16(demultiplexer_1_out16), .out17(demultiplexer_1_out17), .out18(demultiplexer_1_out18),
    .out19(demultiplexer_1_out19), .out20(demultiplexer_1_out20), .out21(demultiplexer_1_out21),
    .out22(demultiplexer_1_out22), .out23(demultiplexer_1_out23), .out24(demultiplexer_1_out24),
    .out25(demultiplexer_1_out25), .out26(demultiplexer_1_out26), .out27(demultiplexer_1_out27),
    .out28(demultiplexer_1_out28), .out29(demultiplexer_1_out29), .out30(demultiplexer_1_out30),
    .out31(demultiplexer_1_out31), .in(WE_t), .sel(A3));  // open: out0, en
  Register #(.width(32)) register_1 (.D(Data), .Q(_0));  // open: en, clk, clr
  Register #(.width(32)) register_2 (.D(Data), .Q(_1), .clk(W1));  // open: en, clr
  Register #(.width(32)) register_3 (.D(Data), .Q(_2), .clk(W2), .clr(undriven));  // open: en
  Register #(.width(32)) register_4 (.D(Data), .Q(_3), .clk(W3), .clr(undriven_2));  // open: en
  Register #(.width(32)) register_5 (.D(Data), .Q(_4), .clk(W4), .clr(undriven_3));  // open: en
  or or_1 (W1, reset_t, demultiplexer_1_out1);
  and and_1 (reset_t, clock_1_out, reset);
  Register #(.width(32)) register_6 (.D(Data), .Q(_5), .clk(W5), .clr(undriven_4));  // open: en
  Register #(.width(32)) register_7 (.D(Data), .Q(_6), .clk(W6), .clr(undriven_5));  // open: en
  Register #(.width(32)) register_8 (.D(Data), .Q(_7), .clk(W7), .clr(undriven_6));  // open: en
  Register #(.width(32)) register_9 (.D(Data), .Q(_8), .clk(W8), .clr(undriven_7));  // open: en
  Register #(.width(32)) register_10 (.D(Data), .Q(_9), .clk(W9), .clr(undriven_8));  // open: en
  or or_2 (W2, reset_t, demultiplexer_1_out2);
  Register #(.width(32)) register_11 (.D(Data), .Q(_10), .clk(W10), .clr(undriven_9));  // open: en
  Register #(.width(32)) register_12 (.D(Data), .Q(_11), .clk(W11), .clr(undriven_10));  // open: en
  Register #(.width(32)) register_13 (.D(Data), .Q(_12), .clk(W12), .clr(undriven_11));  // open: en
  Register #(.width(32)) register_14 (.D(Data), .Q(_13), .clk(W13), .clr(undriven_12));  // open: en
  Register #(.width(32)) register_15 (.D(Data), .Q(_14), .clk(W14), .clr(undriven_13));  // open: en
  or or_3 (W3, reset_t, demultiplexer_1_out3);
  Register #(.width(32)) register_16 (.D(Data), .Q(_15), .clk(W15), .clr(undriven_14));  // open: en
  Register #(.width(32)) register_17 (.D(Data), .Q(_16), .clk(W16), .clr(undriven_15));  // open: en
  Register #(.width(32)) register_18 (.D(Data), .Q(_17), .clk(W17), .clr(undriven_16));  // open: en
  Register #(.width(32)) register_19 (.D(Data), .Q(_18), .clk(W18), .clr(undriven_17));  // open: en
  Register #(.width(32)) register_20 (.D(Data), .Q(_19), .clk(W19), .clr(undriven_18));  // open: en
  or or_4 (W4, reset_t, demultiplexer_1_out4);
  and and_2 (WE_t, clock_1_out, WE);
  Register #(.width(32)) register_21 (.D(Data), .Q(_20), .clk(W20), .clr(undriven_19));  // open: en
  Register #(.width(32)) register_22 (.D(Data), .Q(_21), .clk(W21), .clr(undriven_20));  // open: en
  Register #(.width(32)) register_23 (.D(Data), .Q(_22), .clk(W22), .clr(undriven_21));  // open: en
  Register #(.width(32)) register_24 (.D(Data), .Q(_23), .clk(W23), .clr(undriven_22));  // open: en
  Register #(.width(32)) register_25 (.D(Data), .Q(_24), .clk(W24), .clr(undriven_23));  // open: en
  Register #(.width(32)) register_26 (.D(Data), .Q(_25), .clk(W25), .clr(undriven_24));  // open: en
  Register #(.width(32)) register_27 (.D(Data), .Q(_26), .clk(W26), .clr(undriven_25));  // open: en
  Register #(.width(32)) register_28 (.D(Data), .Q(_27), .clk(W27), .clr(undriven_26));  // open: en
  Register #(.width(32)) register_29 (.D(Data), .Q(_28), .clk(W28), .clr(undriven_27));  // open: en
  Register #(.width(32)) register_30 (.D(Data), .Q(_29), .clk(W29), .clr(undriven_28));  // open: en
  or or_5 (W5, reset_t, demultiplexer_1_out5);
  or or_6 (W6, reset_t, demultiplexer_1_out6);
  Register #(.width(32)) register_31 (.D(Data), .Q(_30), .clk(W30), .clr(undriven_29));  // open: en
  Register #(.width(32)) register_32 (.D(Data), .Q(_31), .clk(W31), .clr(undriven_30));  // open: en
  or or_7 (W7, reset_t, demultiplexer_1_out7);
  or or_8 (W8, reset_t, demultiplexer_1_out8);
  Multiplexer #(.select(5), .width(32)) multiplexer_2 (
    .in0(_0), .in1(_1), .in2(_2), .in3(_3), .in4(_4), .in5(_5), .in6(_6), .in7(_7), .in8(_8), .in9(_9),
    .in10(_10), .in11(_11), .in12(_12), .in13(_13), .in14(_14), .in15(_15), .in16(_16), .in17(_17),
    .in18(_18), .in19(_19), .in20(_20), .in21(_21), .in22(_22), .in23(_23), .in24(_24), .in25(_25),
    .in26(_26), .in27(_27), .in28(_28), .in29(_29), .in30(_30), .in31(_31), .out(out_7), .sel(A1));  // open: en
  Multiplexer #(.select(5), .width(32)) multiplexer_3 (
    .in0(_0), .in1(_1), .in2(_2), .in3(_3), .in4(_4), .in5(_5), .in6(_6), .in7(_7), .in8(_8), .in9(_9),
    .in10(_10), .in11(_11), .in12(_12), .in13(_13), .in14(_14), .in15(_15), .in16(_16), .in17(_17),
    .in18(_18), .in19(_19), .in20(_20), .in21(_21), .in22(_22), .in23(_23), .in24(_24), .in25(_25),
    .in26(_26), .in27(_27), .in28(_28), .in29(_29), .in30(_30), .in31(_31), .out(out_8), .sel(A2));  // open: en
  or or_9 (W9, reset_t, demultiplexer_1_out9);
  or or_10 (W10, reset_t, demultiplexer_1_out10);
  or or_11 (W11, reset_t, demultiplexer_1_out11);
  or or_12 (W12, reset_t, demultiplexer_1_out12);
  or or_13 (W13, reset_t, demultiplexer_1_out13);
  or or_14 (W14, reset_t, demultiplexer_1_out14);
  or or_15 (W15, reset_t, demultiplexer_1_out15);
  or or_16 (W16, reset_t, demultiplexer_1_out16);
  or or_17 (W17, reset_t, demultiplexer_1_out17);
  or or_18 (W18, reset_t, demultiplexer_1_out18);
  or or_19 (W19, reset_t, demultiplexer_1_out19);
  or or_20 (W20, reset_t, demultiplexer_1_out20);
  or or_21 (W21, reset_t, demultiplexer_1_out21);
  or or_22 (W22, reset_t, demultiplexer_1_out22);
  or or_23 (W23, reset_t, demultiplexer_1_out23);
  or or_24 (W24, reset_t, demultiplexer_1_out24);
  or or_25 (W25, reset_t, demultiplexer_1_out25);
  or or_26 (W26, reset_t, demultiplexer_1_out26);
  or or_27 (W27, reset_t, demultiplexer_1_out27);
  or or_28 (W28, reset_t, demultiplexer_1_out28);
  or or_29 (W29, reset_t, demultiplexer_1_out29);
  or or_30 (W30, reset_t, demultiplexer_1_out30);
  or or_31 (W31, reset_t, demultiplexer_1_out31);

  // Other names for the same wires on the sheet: r = reset
endmodule
