// Logisim project CPU.circ as structural Verilog: 11 circuits, main circuit main
module main (
  input  in_1,
  output [31:0] out_2,
  output out_3,
  output [4:0] out_4,
  output [31:0] out_5,
  output out_6,
  output [4:0] out_7,
  output [31:0] out_8
);

  CPU cpu_1 (
    .Reset(in_1), .out_2(out_2), .out_3(out_3), .out_4(out_4), .out_5(out_5), .out_6(out_6), .out_7(out_7),
    .out_8(out_8));
endmodule

module GRF (
  input  clk,
  input  reset,
  input  WE,
  input  [4:0] A1,
  input  [4:0] A2,
  input  [4:0] A3,
  input  [31:0] Data,
  output [31:0] RD1,
  output [31:0] RD2
);

  wire W1, W2, W3, W4, W5, W6, W7, W8, W9, W10, W11, W12, W13, W14, W15, W16, W17, W18, W19, W20, W21, W22,
       W23, W24, W25, W26, W27, W28, W29, W30, W31;
  wire [31:0] _0, _1, _2, _3, _4, _5, _6, _7, _8, _9, _10, _11, _12, _13, _14, _15, _16, _17, _18, _19, _20,
       _21, _22, _23, _24, _25, _26, _27, _28, _29, _30, _31;

  Register #(.width(32)) register_1 (.D(Data), .en(1'b0), .Q(_0), .clk(clk), .clr(reset));
  Register #(.width(32)) register_2 (.D(Data), .en(W1), .Q(_1), .clk(clk), .clr(reset));
  Register #(.width(32)) register_3 (.D(Data), .en(W2), .Q(_2), .clk(clk), .clr(reset));
  Register #(.width(32)) register_4 (.D(Data), .en(W3), .Q(_3), .clk(clk), .clr(reset));
  Register #(.width(32)) register_5 (.D(Data), .en(W4), .Q(_4), .clk(clk), .clr(reset));
  Demultiplexer #(.select(5)) demultiplexer_1 (
    .out1(W1), .out2(W2), .out3(W3), .out4(W4), .out5(W5), .out6(W6), .out7(W7), .out8(W8), .out9(W9),
    .out10(W10), .out11(W11), .out12(W12), .out13(W13), .out14(W14), .out15(W15), .out16(W16), .out17(W17),
    .out18(W18), .out19(W19), .out20(W20), .out21(W21), .out22(W22), .out23(W23), .out24(W24), .out25(W25),
    .out26(W26), .out27(W27), .out28(W28), .out29(W29), .out30(W30), .out31(W31), .in(WE), .sel(A3));  // open: out0, en
  Register #(.width(32)) register_6 (.D(Data), .en(W5), .Q(_5), .clk(clk), .clr(reset));
  Register #(.width(32)) register_7 (.D(Data), .en(W6), .Q(_6), .clk(clk), .clr(reset));
  Register #(.width(32)) register_8 (.D(Data), .en(W7), .Q(_7), .clk(clk), .clr(reset));
  Register #(.width(32)) register_9 (.D(Data), .en(W8), .Q(_8), .clk(clk), .clr(reset));
  Register #(.width(32)) register_10 (.D(Data), .en(W9), .Q(_9), .clk(clk), .clr(reset));
  Register #(.width(32)) register_11 (.D(Data), .en(W10), .Q(_10), .clk(clk), .clr(reset));
  Register #(.width(32)) register_12 (.D(Data), .en(W11), .Q(_11), .clk(clk), .clr(reset));
  Register #(.width(32)) register_13 (.D(Data), .en(W12), .Q(_12), .clk(clk), .clr(reset));
  Register #(.width(32)) register_14 (.D(Data), .en(W13), .Q(_13), .clk(clk), .clr(reset));
  Register #(.width(32)) register_15 (.D(Data), .en(W14), .Q(_14), .clk(clk), .clr(reset));
  Register #(.width(32)) register_16 (.D(Data), .en(W15), .Q(_15), .clk(clk), .clr(reset));
  Register #(.width(32)) register_17 (.D(Data), .en(W16), .Q(_16), .clk(clk), .clr(reset));
  Register #(.width(32)) register_18 (.D(Data), .en(W17), .Q(_17), .clk(clk), .clr(reset));
  Register #(.width(32)) register_19 (.D(Data), .en(W18), .Q(_18), .clk(clk), .clr(reset));
  Register #(.width(32)) register_20 (.D(Data), .en(W19), .Q(_19), .clk(clk), .clr(reset));
  Register #(.width(32)) register_21 (.D(Data), .en(W20), .Q(_20), .clk(clk), .clr(reset));
  Register #(.width(32)) register_22 (.D(Data), .en(W21), .Q(_21), .clk(clk), .clr(reset));
  Register #(.width(32)) register_23 (.D(Data), .en(W22), .Q(_22), .clk(clk), .clr(reset));
  Register #(.width(32)) register_24 (.D(Data), .en(W23), .Q(_23), .clk(clk), .clr(reset));
  Register #(.width(32)) register_25 (.D(Data), .en(W24), .Q(_24), .clk(clk), .clr(reset));
  Register #(.width(32)) register_26 (.D(Data), .en(W25), .Q(_25), .clk(clk), .clr(reset));
  Register #(.width(32)) register_27 (.D(Data), .en(W26), .Q(_26), .clk(clk), .clr(reset));
  Register #(.width(32)) register_28 (.D(Data), .en(W27), .Q(_27), .clk(clk), .clr(reset));
  Register #(.width(32)) register_29 (.D(Data), .en(W28), .Q(_28), .clk(clk), .clr(reset));
  Register #(.width(32)) register_30 (.D(Data), .en(W29), .Q(_29), .clk(clk), .clr(reset));
  Register #(.width(32)) register_31 (.D(Data), .en(W30), .Q(_30), .clk(clk), .clr(reset));
  Register #(.width(32)) register_32 (.D(Data), .en(W31), .Q(_31), .clk(clk), .clr(reset));
  Multiplexer #(.select(5), .width(32)) multiplexer_1 (
    .in0(_0), .in1(_1), .in2(_2), .in3(_3), .in4(_4), .in5(_5), .in6(_6), .in7(_7), .in8(_8), .in9(_9),
    .in10(_10), .in11(_11), .in12(_12), .in13(_13), .in14(_14), .in15(_15), .in16(_16), .in17(_17),
    .in18(_18), .in19(_19), .in20(_20), .in21(_21), .in22(_22), .in23(_23), .in24(_24), .in25(_25),
    .in26(_26), .in27(_27), .in28(_28), .in29(_29), .in30(_30), .in31(_31), .out(RD1), .sel(A1));  // open: en
  Multiplexer #(.select(5), .width(32)) multiplexer_2 (
    .in0(_0), .in1(_1), .in2(_2), .in3(_3), .in4(_4), .in5(_5), .in6(_6), .in7(_7), .in8(_8), .in9(_9),
    .in10(_10), .in11(_11), .in12(_12), .in13(_13), .in14(_14), .in15(_15), .in16(_16), .in17(_17),
    .in18(_18), .in19(_19), .in20(_20), .in21(_21), .in22(_22), .in23(_23), .in24(_24), .in25(_25),
    .in26(_26), .in27(_27), .in28(_28), .in29(_29), .in30(_30), .in31(_31), .out(RD2), .sel(A2));  // open: en
endmodule

module ALU (
  input  [3:0] ALUCtrl,
  input  [31:0] SrcA,
  input  [31:0] SrcB,
  output Zero,
  output [31:0] ALURes
);

  wire [0:0] R8, R9;
  wire [31:0] R0, R1, R2, R3, R4, R5, R6;

  Adder #(.width(32)) adder_1 (.a(SrcA), .b(SrcB), .out(R0));  // open: cin, cout
  Subtractor #(.width(32)) subtractor_1 (.a(SrcA), .b(SrcB), .out(R1));  // open: bin, bout
  assign R2 = SrcA & SrcB;  // AND_Gate and_1, 32 bits wide
  assign R3 = SrcA | SrcB;  // OR_Gate or_1, 32 bits wide
  Shifter #(.width(32)) shifter_1 (.in(SrcB), .\dist (SrcA[4:0]), .out(R4));
  Shifter #(.width(32), .shift("lr")) shifter_2 (.in(SrcB), .\dist (SrcA[4:0]), .out(R5));
  Multiplexer #(.select(4), .width(32)) multiplexer_1 (
    .in0(R0), .in1(R1), .in2(R2), .in3(R3), .in4(R4), .in5(R5), .in6(R6), .in7({SrcB[15:0], {16{1'b0}}}),
    .in8({{31{1'b0}}, R8[0]}), .in9({{31{1'b0}}, R9[0]}), .out(ALURes), .sel(ALUCtrl));  // open: in10, in11, in12, in13, in14, in15, en
  Shifter #(.width(32), .shift("ar")) shifter_3 (.in(SrcB), .\dist (SrcA[4:0]), .out(R6));
  // Probe on ALURes
  Comparator #(.width(32), .mode("unsigned")) comparator_1 (.a({32{1'b0}}), .b(ALURes), .eq(Zero));  // open: gt, lt
  Comparator #(.width(32), .mode("unsigned")) comparator_2 (.a(SrcA), .b(SrcB), .lt(R8[0]));  // open: gt, eq
  Comparator #(.width(32)) comparator_3 (.a(SrcA), .b(SrcB), .lt(R9[0]));  // open: gt, eq

  // Other names for the same wires on the sheet: R7[31:16] = SrcB[15:0]
endmodule

module EXT (
  input  [15:0] Imm,
  input  ExtOp,
  output [31:0] ExtRes
);

  wire [31:16] \signed ;

  Multiplexer #(.width(16)) multiplexer_1 (
    .in0({16{1'b0}}), .in1({16{1'b1}}), .out(\signed ), .sel(Imm[15]));  // open: en
  Multiplexer #(.width(32)) multiplexer_2 (
    .in0({{16{1'b0}}, Imm}), .in1({\signed , Imm}), .out(ExtRes), .sel(ExtOp));  // open: en

  // Other names for the same wires on the sheet: signed[15:0] = Imm; zero[15:0] = Imm
endmodule

module DM (
  input  Clk,
  input  WE,
  input  Reset,
  input  [31:0] Addr,
  input  [31:0] Data,
  output [31:0] RD,
  output [4:0] out_7
);

  RAM #(.addrWidth(5), .dataWidth(32), .bus("separate")) ram_1 (
    .addr(Addr[6:2]), .din(Data), .data(RD), .str(WE), .clk(Clk), .clr(Reset));  // open: sel, ld

  assign out_7 = Addr[6:2];

  // Other names for the same wires on the sheet: Addr_t[4:0] = Addr[6:2]
endmodule

module IFU (
  input  PCSrc,
  input  Clk,
  input  Reset,
  input  Jump,
  input  Jump_R,
  input  [15:0] Imm,
  input  [25:0] J_Addr,
  input  [31:0] RD,
  output [31:0] Inst,
  output [31:0] PC_4
);

  wire [27:0] PC;
  wire [31:0] ext_1_extres, multiplexer_1_out, multiplexer_2_out, multiplexer_3_out, nPC_B, shifter_1_out;
  wire [31:28] nPC_J;

  Multiplexer #(.width(32)) multiplexer_1 (.in0(PC_4), .in1(nPC_B), .out(multiplexer_1_out), .sel(PCSrc));  // open: en
  Multiplexer #(.width(32)) multiplexer_2 (
    .in0(multiplexer_1_out), .in1({nPC_J, J_Addr, 2'b00}), .out(multiplexer_2_out), .sel(Jump));  // open: en
  Multiplexer #(.width(32)) multiplexer_3 (
    .in0(multiplexer_2_out), .in1(RD), .out(multiplexer_3_out), .sel(Jump_R));  // open: en
  Register #(.width(32)) u_PC (.D(multiplexer_3_out), .Q({nPC_J, PC}), .clk(Clk), .clr(Reset));  // open: en
  Adder #(.width(32)) adder_1 (.a({nPC_J, PC}), .b(32'h4), .out(PC_4));  // open: cin, cout
  ROM #(.addrWidth(5), .dataWidth(32)) rom_1 (.addr(PC[6:2]), .data(Inst));  // open: sel
  EXT ext_1 (.Imm(Imm), .ExtOp(1'b1), .ExtRes(ext_1_extres));
  Shifter #(.width(32)) shifter_1 (.in(ext_1_extres), .\dist (5'b00010), .out(shifter_1_out));
  Adder #(.width(32)) adder_2 (.a(PC_4), .b(shifter_1_out), .out(nPC_B));  // open: cin, cout

  // Other names for the same wires on the sheet: nPC_J[27:2] = J_Addr; PC[31:28] = nPC_J
endmodule

module Controlller (
  input  [5:0] Op,
  input  [5:0] Funct,
  output MemtoReg,
  output MemWrite,
  output Branch,
  output [3:0] BranchOp,
  output [3:0] ALUCtrl,
  output ALUSrc,
  output RegDst,
  output RegWrite,
  output Extend,
  output ALUASrc,
  output Jump,
  output Jump_R,
  output Link
);

  wire addu, beq, j, jal, jalr, jr, lui, lw, not_1_out, not_2_out, not_3_out, not_4_out, not_5_out,
       not_6_out, not_7_out, not_8_out, not_9_out, not_10_out, not_11_out, not_12_out, or_9_out, or_11_out,
       or_12_out, or_14_out, or_15_out, or_17_out, or_18_out, or_19_out, ori, R, sll, sllv, sra, srav, srl,
       srlv, subu, sw;
  wire [3:0] multiplexer_1_out, multiplexer_2_out, multiplexer_3_out, multiplexer_4_out, multiplexer_5_out,
       multiplexer_6_out;

  not not_1 (not_1_out, Op[5]);
  buf or_1 (MemtoReg, lw);  // OR_Gate
  not not_2 (not_2_out, Op[4]);
  not not_3 (not_3_out, Op[3]);
  not not_4 (not_4_out, Op[2]);
  buf or_2 (MemWrite, sw);  // OR_Gate
  not not_5 (not_5_out, Op[1]);
  not not_6 (not_6_out, Op[0]);
  buf or_3 (Branch, beq);  // OR_Gate
  and u_R (R, not_1_out, not_2_out, not_3_out, not_4_out, not_5_out, not_6_out);
  and u_ori (ori, not_1_out, not_2_out, Op[3], Op[2], not_5_out, Op[0]);
  and u_lw (lw, Op[5], not_2_out, not_3_out, not_4_out, Op[1], Op[0]);
  and u_sw (sw, Op[5], not_2_out, Op[3], not_4_out, Op[1], Op[0]);
  and u_beq (beq, not_1_out, not_2_out, not_3_out, Op[2], not_5_out, not_6_out);
  and u_lui (lui, not_1_out, not_2_out, Op[3], Op[2], Op[1], Op[0]);
  and u_j (j, not_1_out, not_2_out, not_3_out, not_4_out, Op[1], not_6_out);
  and u_jal (jal, not_1_out, not_2_out, not_3_out, not_4_out, Op[1], Op[0]);
  or or_4 (ALUSrc, ori, lw, sw, lui);
  or or_5 (RegDst, srlv, sll, addu, subu, jr, jalr, sllv, sra, srav, srl);
  not not_7 (not_7_out, Funct[4]);
  not not_8 (not_8_out, Funct[5]);
  not not_9 (not_9_out, Funct[2]);
  not not_10 (not_10_out, Funct[3]);
  or or_6 (RegWrite, addu, subu, ori, lw, lui, sll, jal, jalr, sllv, sra, srav, srl, srlv);
  not not_11 (not_11_out, Funct[1]);
  not not_12 (not_12_out, Funct[0]);
  or or_7 (Extend, lw, sw, beq, lui);
  and R_2 (addu, Funct[5], not_7_out, not_10_out, not_9_out, not_11_out, Funct[0], R);
  and R_3 (subu, Funct[5], not_7_out, not_10_out, not_9_out, Funct[1], Funct[0], R);
  and R_4 (sll, not_8_out, not_7_out, not_10_out, not_9_out, not_11_out, not_12_out, R);
  and R_5 (jr, not_8_out, not_7_out, Funct[3], not_9_out, not_11_out, not_12_out, R);
  and R_6 (jalr, not_8_out, not_7_out, Funct[3], not_9_out, not_11_out, Funct[0], R);
  and R_7 (sllv, not_8_out, not_7_out, not_10_out, Funct[2], not_11_out, not_12_out, R);
  and R_8 (sra, not_8_out, not_7_out, not_10_out, not_9_out, Funct[1], Funct[0], R);
  and R_9 (srav, not_8_out, not_7_out, not_10_out, Funct[2], Funct[1], Funct[0], R);
  and R_10 (srl, not_8_out, not_7_out, not_10_out, not_9_out, Funct[1], not_12_out, R);
  and R_11 (srlv, not_8_out, not_7_out, not_10_out, Funct[2], Funct[1], not_12_out, R);
  or or_8 (ALUASrc, sll, sra, srl);
  or or_9 (or_9_out, srl, srlv);
  or or_10 (Jump, j, jal);
  Multiplexer #(.width(4)) multiplexer_1 (
    .in0(4'b0000), .in1(4'b0101), .out(multiplexer_1_out), .sel(or_9_out));  // open: en
  Multiplexer #(.width(4)) multiplexer_2 (
    .in0(multiplexer_1_out), .in1(4'b0110), .out(multiplexer_2_out), .sel(or_11_out));  // open: en
  or or_11 (or_11_out, sra, srav);
  Multiplexer #(.width(4)) multiplexer_3 (
    .in0(multiplexer_2_out), .in1(4'b0100), .out(multiplexer_3_out), .sel(or_12_out));  // open: en
  or or_12 (or_12_out, sll, sllv);
  or or_13 (Jump_R, jr, jalr);
  Multiplexer #(.width(4)) multiplexer_4 (
    .in0(multiplexer_3_out), .in1(4'b0111), .out(multiplexer_4_out), .sel(or_14_out));  // open: en
  buf or_14 (or_14_out, lui);  // OR_Gate
  buf or_15 (or_15_out, ori);  // OR_Gate
  or or_16 (Link, jal, jalr);
  Multiplexer #(.width(4)) multiplexer_5 (
    .in0(multiplexer_4_out), .in1(4'b0011), .out(multiplexer_5_out), .sel(or_15_out));  // open: en
  Multiplexer #(.width(4)) multiplexer_6 (
    .in0(multiplexer_5_out), .in1(4'b0001), .out(multiplexer_6_out), .sel(or_17_out));  // open: en
  buf or_17 (or_17_out, subu);  // OR_Gate
  or or_18 (or_18_out, lw, addu, sw);
  Multiplexer #(.width(4)) multiplexer_7 (
    .in0(multiplexer_6_out), .in1(4'b0000), .out(ALUCtrl), .sel(or_18_out));  // open: en
  buf or_19 (or_19_out, beq);  // OR_Gate
  Multiplexer #(.width(4)) multiplexer_8 (.in0(4'b0000), .in1(4'b0000), .out(BranchOp), .sel(or_19_out));  // open: en

  // Other names for the same wires on the sheet: f0 = Funct[0]; f1 = Funct[1]; f2 = Funct[2]; f3 = Funct[3];
  //   f4 = Funct[4]; f5 = Funct[5]
endmodule

module Inst_Pipeline (
  input  [31:0] in_1,
  output [5:0] Op,
  output [5:0] Funct,
  output [4:0] rs,
  output [4:0] rt,
  output [4:0] rd,
  output [15:0] imm,
  output [25:0] jumpaddress,
  output [4:0] s
);


  assign Funct = in_1[5:0];
  assign imm = in_1[15:0];
  assign jumpaddress = in_1[25:0];
  assign Op = in_1[31:26];
  assign rd = in_1[15:11];
  assign rs = in_1[25:21];
  assign rt = in_1[20:16];
  assign s = in_1[10:6];
endmodule

module Branch (
  input  Branch,
  input  [3:0] BranchOp,
  input  [31:0] SrcA,
  input  [31:0] SrcB,
  output out_5
);

  wire and_1_out, beq, demultiplexer_1_out0, Res;

  Comparator #(.width(32), .mode("unsigned")) comparator_1 (.a(SrcA), .b(SrcB), .eq(beq));  // open: gt, lt
  Demultiplexer #(.select(4)) demultiplexer_1 (
    .out0(demultiplexer_1_out0), .in(1'b1), .sel(BranchOp));  // open: out1, out2, out3, out4, out5, out6, out7, out8, out9, out10, out11, out12, out13, out14, out15, en
  and and_1 (and_1_out, beq, demultiplexer_1_out0);
  buf or_1 (Res, and_1_out);  // OR_Gate
  and and_2 (out_5, Branch, Res);
endmodule

module CPU (
  input  Reset,
  output [31:0] out_2,
  output out_3,
  output [4:0] out_4,
  output [31:0] out_5,
  output out_6,
  output [4:0] out_7,
  output [31:0] out_8
);

  wire ALUASrc, ALUSrc, and_1_out, Branch, Clk, Extend, Jump, Jump_R, Link, MemtoReg, not_1_out, PCSrc,
       RegDst, Zero;
  wire [3:0] ALUCtrl, BranchOp;
  wire [4:0] multiplexer_1_out, rd, rs, rt, s;
  wire [5:0] Funct, Op;
  wire [15:0] imm;
  wire [25:0] j_addr;
  wire [31:0] ALURes, ALUSrcA, ALUSrcB, imm_extend, MemRD, multiplexer_5_out, PC_4, RD1, s_extend;

  Clock clock_1 (.out(Clk));
  assign s_extend = {{27{1'b0}}, s};  // Bit_Extender bit_extender_1
  Inst_Pipeline inst_pipeline_1 (
    .in_1(out_2), .Op(Op), .Funct(Funct), .rs(rs), .rt(rt), .rd(rd), .imm(imm), .jumpaddress(j_addr), .s(s));
  IFU ifu_1 (
    .Imm(imm), .Inst(out_2), .PCSrc(PCSrc), .Clk(Clk), .Reset(Reset), .J_Addr(j_addr), .Jump(Jump),
    .Jump_R(Jump_R), .RD(RD1), .PC_4(PC_4));
  Controlller controlller_1 (
    .Op(Op), .Funct(Funct), .MemtoReg(MemtoReg), .MemWrite(out_6), .Branch(Branch), .BranchOp(BranchOp),
    .ALUCtrl(ALUCtrl), .ALUSrc(ALUSrc), .RegDst(RegDst), .RegWrite(out_3), .Extend(Extend),
    .ALUASrc(ALUASrc), .Jump(Jump), .Jump_R(Jump_R), .Link(Link));
  Multiplexer #(.width(5)) multiplexer_1 (.in0(rt), .in1(rd), .out(multiplexer_1_out), .sel(RegDst));  // open: en
  and and_1 (and_1_out, Link, not_1_out);
  not not_1 (not_1_out, Jump_R);
  GRF grf_1 (.A1(rs), .A2(rt), .A3(out_4), .Data(out_5), .RD1(RD1), .RD2(out_8), .clk(Clk), .reset(Reset), .WE(out_3));
  Multiplexer #(.width(5)) multiplexer_2 (
    .in0(multiplexer_1_out), .in1({5{1'b1}}), .out(out_4), .sel(and_1_out));  // open: en
  Multiplexer #(.width(32)) multiplexer_3 (.in0(RD1), .in1(s_extend), .out(ALUSrcA), .sel(ALUASrc));  // open: en
  Multiplexer #(.width(32)) multiplexer_4 (.in0(out_8), .in1(imm_extend), .out(ALUSrcB), .sel(ALUSrc));  // open: en
  EXT ext_1 (.Imm(imm), .ExtOp(Extend), .ExtRes(imm_extend));
  ALU alu_1 (.SrcA(ALUSrcA), .SrcB(ALUSrcB), .Zero(Zero), .ALURes(ALURes), .ALUCtrl(ALUCtrl));
  Branch branch_1 (.SrcA(ALUSrcA), .SrcB(ALUSrcB), .Branch(Branch), .BranchOp(BranchOp), .out_5(PCSrc));
  Multiplexer #(.width(32)) multiplexer_5 (
    .in0(ALURes), .in1(MemRD), .out(multiplexer_5_out), .sel(MemtoReg));  // open: en
  DM dm_1 (.Addr(ALURes), .Data(out_8), .RD(MemRD), .Clk(Clk), .WE(out_6), .Reset(Reset), .out_7(out_7));
  Multiplexer #(.width(32)) multiplexer_6 (.in0(multiplexer_5_out), .in1(PC_4), .out(out_5), .sel(Link));  // open: en

  // Other names for the same wires on the sheet: Inst[31:0] = out_2; MemAddr[4:0] = out_7; MemWrite = out_6;
  //   MemData[31:0] = out_8; RD2[31:0] = out_8; RegAddr[4:0] = out_4; RegData[31:0] = out_5; RegWrite = out_3
endmodule

module testbench (
  input  in_1,
  output [31:0] out_2,
  output out_3,
  output [4:0] out_4,
  output [31:0] out_5,
  output out_6,
  output [4:0] out_7,
  output [31:0] out_8
);

  wire clock_1_out, comparator_1_gt;
  wire [7:0] counter_1_q;

  Clock clock_1 (.out(clock_1_out));
  Counter counter_1 (.Q(counter_1_q), .carry(in_1), .clk(clock_1_out));  // open: load, D, count, clr
  Comparator comparator_1 (.a(8'h4), .b(counter_1_q), .gt(comparator_1_gt));  // open: eq, lt
  main main_1 (
    .in_1(comparator_1_gt), .out_2(out_2), .out_3(out_3), .out_4(out_4), .out_5(out_5), .out_6(out_6),
    .out_7(out_7), .out_8(out_8));
  // Probe on out_2
endmodule
